# Fritzing sketch Money Counter Schematic (saved by Fritzing 0.9.4)
breadboards: 1

parts:
  M1 = Stepper Motor - Bipolar
  IC1 = ULN2003A [package="DIP16 [THT]"]
  5V_DC_Power_Supply = Power plug
  Part1 = Arduino Uno (Rev3)
  4x4_Keypad = KEYPAD 4x4

nets:
  N1: M1.A, IC1.Out_1
  N2: M1.C, IC1.Out_2
  N3: M1.B, IC1.Out_3
  N4: M1.D, IC1.Out_4
  N5: IC1.In_1, Part1.D10_PWM/SS
  N6: IC1.In_2, Part1.D11_PWM/MOSI
  N7: IC1.In_3, Part1.D12/MISO
  N8: IC1.In_4, Part1.D13/SCK
  N9: IC1.In_7, 5V_DC_Power_Supply.VCC
  N10: IC1.0V, 5V_DC_Power_Supply.GND
  N11: Part1.D8, 4x4_Keypad.row2
  N12: Part1.D9_PWM, 4x4_Keypad.row1
  N13: Part1.D2, 4x4_Keypad.col4
  N14: Part1.D3_PWM, 4x4_Keypad.col3
  N15: Part1.D4, 4x4_Keypad.col2
  N16: Part1.D5_PWM, 4x4_Keypad.col1
  N17: Part1.D6_PWM, 4x4_Keypad.row4
  N18: Part1.D7, 4x4_Keypad.row3

custom parts:
  KEYPAD 4x4: Matrix keypad 16 buttons, 4 rows x 4 columns
